# Fritzing sketch Mackie breadboard (saved by Fritzing 0.9.9b)
breadboards: 1

parts:
  Part1 = Arduino Pro Micro (Clone)
  S1 = Pushbutton [package="[THT]"]
  S2 = Pushbutton [package="[THT]"]
  S3 = Pushbutton [package="[THT]"]
  R1 = Rotary Potentiometer (Small) [maximum_resistance=100kΩ package=THT]
  RE1 = Rotary Encoder [package=THT]
  RE2 = Rotary Encoder [package=THT]
  R2 = Rotary Potentiometer (Small) [maximum_resistance=100kΩ package=THT]
  R3 = Rotary Potentiometer (Small) [maximum_resistance=100kΩ package=THT]

nets:
  N1: Part1.D2, S1.Pin_1, S1.Pin_2
  N2: Part1.D3, S2.Pin_1, S2.Pin_2
  N3: Part1.D4, S3.Pin_1, S3.Pin_2
  N4: Part1.D10, RE1.EncoderPinB
  N5: Part1.D16, RE1.EncoderPinA
  N6: Part1.D14, RE2.EncoderPinB
  N7: Part1.D15, RE2.EncoderPinA
  N8: Part1.A0, R1.wiper
  N9: Part1.A1, R2.wiper
  N10: Part1.A2, R3.wiper
  N11: S1.Pin_3, S1.Pin_4, S2.Pin_3, S2.Pin_4, S3.Pin_3, S3.Pin_4, R1.leg1, RE1.EncoderPinC, RE2.EncoderPinC, R2.leg1, R3.leg1, R3.leg2
  N12: R1.leg2, R2.leg2

notes:
  Pot B10k
  Encoder
