# Fritzing sketch one_fader_test (saved by Fritzing 0.9.3b)
breadboards: 1

parts:
  IC1 = L293D [package=THT]
  Part1 = Arduino Uno (Rev3)
  U1 = SLIDER [package=slider]
  M1 = DC Motor
  U2 = POT [package=alps_pot]
  R1 = Resistor [tolerance=±5% resistance=1M package="2010 [SMD]"]
  VCC1 = Battery block 9V
  C1 = Electrolytic Capacitor [capacitance=10µF package="100 mil [THT, electrolytic]"]

nets:
  N1: IC1.Enable_1, Part1.D9_PWM
  N2: IC1.In_1, Part1.D2
  N3: IC1.Out_1_(_Controlled_by_Enable_1_), M1.pin_1
  N4: IC1.0V, Part1.GND, U1.E, U2.E, VCC1.-, C1.-
  N5: IC1.Out_2_(_Controlled_by_Enable_1_), M1.pin_2
  N6: IC1.In_2, Part1.D3_PWM
  N7: IC1.+Vmotor, VCC1.+
  N8: IC1.+V, Part1.5V, U1.A, U2.A, C1.+
  N9: Part1.A0, U1.S
  N10: Part1.A1, U2.S
  N11: Part1.D8, R1.Pin_0
  N12: Part1.D7, R1.Pin_1

notes:
  Fade Touch Line
  1M ohm
  10uF
  by Gustavo Silveira
  musiconerd.com
