# Fritzing sketch MIDI in (saved by Fritzing 0.9.9b)
breadboards: 1

parts:
  Part1 = Arduino Uno (Rev3)
  D1 = Diode [package=diode-1n4148]
  U1 = OPTO_DARL_6N138S [package=8-smd]
  DIN2 = DIN-5 jack (MIDI) [package=THT]
  R2 = Resistor [tolerance=±5% power=0.25 resistance=220 package=THT]
  R3 = Resistor [tolerance=±5% power=0.25 resistance=4.7 package=THT]
  R4 = Resistor [tolerance=±5% power=0.25 resistance=220 package=THT]

nets:
  N1: Part1.D0/RX, U1.VOUT, R2.Pin_1
  5V: Part1.5V, U1.VCC, R2.Pin_0
  GND: Part1.GND, U1.GND, R3.Pin_0
  N2: D1.A, U1.C, DIN2.5
  N3: D1.C, U1.A, R4.Pin_0
  N4: DIN2.4, R4.Pin_1

notes:
  This is the front of the connector
  Pin order:
  3 - 5- 2- 4 - 1
  220 Ohm
  4.7K
