# Fritzing sketch MIDI out (saved by Fritzing 0.9.9b)

parts:
  DIN1 = DIN-5 jack (MIDI) [package=THT]
  Part1 = Arduino Uno (Rev3)
  R1 = Resistor [tolerance=±5% power=0.25 resistance=220 package=THT]

nets:
  N1: DIN1.5, Part1.D1/TX
  N2: DIN1.2, Part1.GND
  N3: DIN1.4, R1.Pin_0
  N4: Part1.5V, R1.Pin_1

notes:
  This is the front of the connector
  Pin order:
  3 - 5- 2- 4 - 1
  220 Ohm
