# Fritzing sketch Full Code - Breadboard (saved by Fritzing 0.9.3b)
breadboards: 2

parts:
  Pro_Micro3 = Pro Micro  # not connected
  Part1 = Analog Digital MUX Breakout  # not connected
  R1 = TRIMPOT [package=3386u]
  R2 = TRIMPOT [package=3386u]
  S1 = Momentary Switch [package=ksa_sealed_tac_switch]
  S2 = Momentary Switch [package=ksa_sealed_tac_switch]
  RE1 = Rotary Encoder [package=THT]
  RE2 = Rotary Encoder [package=THT]
  OLED1 = OLED 128x64 I2C Monochrome Display
  R3 = Rotary Potentiometer (Small) [maximum_resistance=100kΩ package=THT]
  R4 = Rotary Potentiometer (Small) [maximum_resistance=100kΩ package=THT]
  S3 = Momentary Switch [package=ksa_sealed_tac_switch]
  S4 = Momentary Switch [package=ksa_sealed_tac_switch]
  S5 = Momentary Switch [package=ksa_sealed_tac_switch]
  S6 = Momentary Switch [package=ksa_sealed_tac_switch]
  U1 = WS2812 RGB LED strip
  U2 = WS2812 RGB LED strip  # not connected
  J3 = Power Jack [package=power_jack_slot]
  R5 = Resistor [tolerance=±5% resistance=330 package="2010 [SMD]"]

nets:
  GND: R1.CCW, R2.CCW, S1.3, S2.3, RE1.EncoderPinC, RE2.EncoderPinC, OLED1.GND, R3.leg1, R4.leg1, S3.4, S4.4, S5.4, S6.4, U1.GND, J3.GND, J3.tip_GND
  VDD: R1.CW, R2.CW, OLED1.VDD, R3.leg2, R4.leg2, U1.VCC, J3.PWR, J3.tip_PWR
  N1: U1.DIN, R5.Pin_0

notes:
  Trimpot b10k
  Rotary Encocoder
  Oled Display
  Arduino Pro Micro
  74hc4067
  breakout
  Tactile Switch
  Potentiometer b10k
  Adressable LED Strip (ws2812)
  5v Power Supply
  330 Ohms

custom parts:
  Pro Micro: The SparkFun Pro Micro is a complete USB-based microcontoller development system, in a very small footprint, capable of implementing many types of projects. All programming can be done via the USB port.
  Rotary Encoder: Rotary Encoder from ALPSec11e with switch.
  WS2812 RGB LED strip: WS2812 strip
  Power Jack: Power Jack This is the standard 5.5mm barrel jack for power. Ths one is modified to mate with the barrel plug part and allow the two to "connect" so batteries and wall warts can be "connected" in breadboard and will go through to schematic.
