# Fritzing sketch Full Code - Breadboard - Leds (saved by Fritzing 0.9.3b)
breadboards: 3

parts:
  Pro_Micro3 = Pro Micro  # not connected
  Part1 = Analog Digital MUX Breakout  # not connected
  S1 = Momentary Switch [package=ksa_sealed_tac_switch]
  S2 = Momentary Switch [package=ksa_sealed_tac_switch]
  RE1 = Rotary Encoder [package=THT]
  RE2 = Rotary Encoder [package=THT]
  OLED1 = OLED 128x64 I2C Monochrome Display
  R3 = Rotary Potentiometer (Small) [maximum_resistance=100kΩ package=THT]
  R4 = Rotary Potentiometer (Small) [maximum_resistance=100kΩ package=THT]
  S3 = Momentary Switch [package=ksa_sealed_tac_switch]
  S4 = Momentary Switch [package=ksa_sealed_tac_switch]
  S5 = Momentary Switch [package=ksa_sealed_tac_switch]
  S6 = Momentary Switch [package=ksa_sealed_tac_switch]
  U1 = 74HC595 [package="DIP16 [THT]"]
  U2 = 74HC595 [package="DIP16 [THT]"]
  LED1 = LED - 3mm [color="Green (555nm)" package="3 mm [THT]"]
  R5 = Resistor [tolerance=±5% resistance=220 package="1206 [SMD]"]
  R6 = Resistor [tolerance=±5% resistance=220 package="1206 [SMD]"]
  R7 = Resistor [tolerance=±5% resistance=220 package="1206 [SMD]"]
  R8 = Resistor [tolerance=±5% resistance=220 package="1206 [SMD]"]
  R9 = Resistor [tolerance=±5% resistance=220 package="1206 [SMD]"]
  R10 = Resistor [tolerance=±5% resistance=220 package="1206 [SMD]"]
  R11 = Resistor [tolerance=±5% resistance=220 package="1206 [SMD]"]
  R12 = Resistor [tolerance=±5% resistance=220 package="1206 [SMD]"]
  R13 = Resistor [tolerance=±5% resistance=220 package="1206 [SMD]"]
  R14 = Resistor [tolerance=±5% resistance=220 package="1206 [SMD]"]
  R15 = Resistor [tolerance=±5% resistance=220 package="1206 [SMD]"]
  R16 = Resistor [tolerance=±5% resistance=220 package="1206 [SMD]"]
  LED15 = LED - 3mm [color="Green (555nm)" package="3 mm [THT]"]
  LED16 = LED - 3mm [color="Green (555nm)" package="3 mm [THT]"]
  LED17 = LED - 3mm [color="Green (555nm)" package="3 mm [THT]"]
  LED18 = LED - 3mm [color="Yellow (595nm)" package="3 mm [THT]"]
  LED19 = LED - 3mm [color="Green (555nm)" package="3 mm [THT]"]
  LED20 = LED - 3mm [color="Red (633nm)" package="3 mm [THT]"]
  LED21 = LED - 3mm [color="Green (555nm)" package="3 mm [THT]"]
  LED22 = LED - 3mm [color="Green (555nm)" package="3 mm [THT]"]
  LED23 = LED - 3mm [color="Green (555nm)" package="3 mm [THT]"]
  LED24 = LED - 3mm [color="Yellow (595nm)" package="3 mm [THT]"]
  LED25 = LED - 3mm [color="Green (555nm)" package="3 mm [THT]"]
  LED26 = LED - 3mm [color="Green (555nm)" package="3 mm [THT]"]
  LED27 = LED - 3mm [color="Red (633nm)" package="3 mm [THT]"]

nets:
  GND: S1.3, S2.3, RE1.EncoderPinC, RE2.EncoderPinC, OLED1.GND, R3.leg1, R4.leg1, S3.4, S4.4, S5.4, S6.4, U1.GND, U1.OE, U2.GND, U2.OE, LED1.cathode, LED15.cathode, LED16.cathode, LED17.cathode, LED18.cathode, LED19.cathode, LED20.cathode, LED21.cathode, LED22.cathode, LED23.cathode, LED24.cathode, LED25.cathode, LED26.cathode, LED27.cathode
  VCC: OLED1.VDD, R3.leg2, R4.leg2, U1.MR, U1.VCC, U2.MR, U2.VCC
  N1: U1.Q1, R6.Pin_1
  N2: U1.Q2, R7.Pin_1
  N3: U1.Q3, R8.Pin_1
  N4: U1.Q4, R9.Pin_1
  N5: U1.Q5, R11.Pin_1
  N6: U1.Q6, R10.Pin_1
  N7: U1.Q7, R12.Pin_1
  N8: U1.Q7', U2.DS
  N9: U1.SH_CP, U2.SH_CP
  N10: U1.ST_CP, U2.ST_CP
  N11: U1.Q0, R5.Pin_1
  N12: U2.Q1, R16.Pin_1
  N13: U2.Q2, R15.Pin_1
  N14: U2.Q3, R14.Pin_1
  N15: U2.Q0, R13.Pin_1
  N16: LED1.anode, R5.Pin_0
  N17: R6.Pin_0, LED15.anode
  N18: R7.Pin_0, LED16.anode
  N19: R8.Pin_0, LED17.anode
  N20: R9.Pin_0, LED19.anode
  N21: R10.Pin_0, LED20.anode
  N22: R11.Pin_0, LED18.anode
  N23: R12.Pin_0, LED21.anode
  N24: R13.Pin_0, LED22.anode
  N25: R14.Pin_0, LED26.anode
  N26: R15.Pin_0, LED23.anode
  N27: R16.Pin_0, LED25.anode

notes:
  Rotary Encocoder
  Oled Display
  Arduino Pro Micro
  74hc4067
  breakout
  Tactile Switch
  Potentiometer b10k
  220 Ohms (or more)
  Bit Shifter 74HC595

custom parts:
  Pro Micro: The SparkFun Pro Micro is a complete USB-based microcontoller development system, in a very small footprint, capable of implementing many types of projects. All programming can be done via the USB port.
  Rotary Encoder: Rotary Encoder from ALPSec11e with switch.
